# Fritzing sketch ServoWOL (saved by Fritzing 0.9.3b)
breadboards: 1

parts:
  Part1 = Arduino Due (Rev2b)
  Raspberry_Pi_1 = Raspberry Pi 3 [part_number=RPI-3-V1.2]
  U1 = 555 Timer [package="DIP8 [THT]"]
  IC1 = Hex Inverter Schmitt Trigger SN74HC14 [package="DIP (Dual Inline)"]
  Q1 = NPN-Transistor [package="SOT-23 [SMD]"]
  Q2 = NPN-Transistor [package="SOT-23 [SMD]"]
  J1 = Basic Servo
  VCC1 = Battery block 9V
  R1 = Resistor [tolerance=±5% resistance=220 package=THT]
  C1 = Ceramic Capacitor [capacitance=100nF package="100 mil [THT, multilayer]"]
  R2 = Resistor [tolerance=±5% resistance=220 package=THT]
  R3 = Resistor [tolerance=±5% resistance=220 package=THT]

nets:
  5V: Part1.5V, J1.vcc
  GND: Part1.GND, Raspberry_Pi_1.GND, U1.Pin_1, U1.Pin_6, IC1.GND, J1.gnd, VCC1.-, C1.0, R3.Pin_1
  N1: Part1.VIN, Q2.2
  N2: Part1.D9_PWM, J1.pulse
  N3: Part1.D7_PWM, U1.Pin_4
  N4: Raspberry_Pi_1.GIPO17, IC1.3Y, R3.Pin_0
  N5: U1.Pin_2, IC1.3A
  N6: U1.Pin_3, R1.Pin_1
  N7: U1.Pin_5, C1.1
  N8: U1.Pin_8, Q1.1, Q2.1, VCC1.+, R2.Pin_0
  N9: IC1.4Y, IC1.6A
  N10: IC1.VCC, R2.Pin_1
  N11: Q1.2, Q2.0
  N12: Q1.0, R1.Pin_0
